# Fritzing sketch Buzzer (saved by Fritzing 0.9.3b)
breadboards: 1

parts:
  Q2 = Basic FET N-Channel [package="D2Pak [SMD]"]
  R4 = Resistor [tolerance=±5% resistance=2.2k package="2010 [SMD]"]
  F2 = Resettable Fuse PTC [package=ptc]
  J2 = Piezo Speaker

nets:
  N1: Q2.Gate, R4.Pin_1
  N2: Q2.drain, J2.pin1
  N3: F2.1, J2.pin2

notes:
  Battery 12V DC
  - +
  Arduino ouput pin 3 (PWM)
  Arduino GND pin
